# Fritzing sketch Untitled_Sketch (saved by Fritzing 0.9.3b)

parts:
  Composant1 = Arduino Uno (Rev3)  # not connected
  Composant2 = Base Shield V2
  Grove_Rotary_Angle_Sensor_(P)1 = Grove Rotary Angle Sensor (P)

nets:
  N1: Composant2.pin_140, Grove_Rotary_Angle_Sensor_(P)1.SIG
  N2: Composant2.pin_141, Grove_Rotary_Angle_Sensor_(P)1.NC
  N3: Composant2.pin_142, Grove_Rotary_Angle_Sensor_(P)1.VCC
  N4: Composant2.pin_143, Grove_Rotary_Angle_Sensor_(P)1.GND

custom parts:
  Grove Rotary Angle Sensor (P): Rotary potentiometer, Grove connector, panel mount.
